# Fritzing sketch sketch (saved by Fritzing 0.9.4)

parts:
  WeMos_D1_Mini_Relay_Shield_V1 = WeMos D1 Mini Relay Shield V2
  Raspberry_Pi2 = Raspberry Pi B+

nets:
  3V3: WeMos_D1_Mini_Relay_Shield_V1.3V3, Raspberry_Pi2.3v3
  N1: WeMos_D1_Mini_Relay_Shield_V1.D1, Raspberry_Pi2.GPIO18
  N2: WeMos_D1_Mini_Relay_Shield_V1.G, Raspberry_Pi2.GND
